# Fritzing sketch 7-segment-countdown (saved by Fritzing 0.9.3b)
breadboards: 2

parts:
  Part1 = Arduino Uno (Rev3) - ICSP
  DI1 = 7-Segment LED Display [package=THT]
  R1 = Resistor [tolerance=±5% resistance=100 package="0603 [SMD]"]
  R2 = Resistor [tolerance=±5% resistance=100 package="0603 [SMD]"]
  R3 = Resistor [tolerance=±5% resistance=100 package="0603 [SMD]"]
  R4 = Resistor [tolerance=±5% resistance=100 package="0603 [SMD]"]
  R5 = Resistor [tolerance=±5% resistance=100 package="0603 [SMD]"]
  R6 = Resistor [tolerance=±5% resistance=100 package="0603 [SMD]"]
  R7 = Resistor [tolerance=±5% resistance=100 package="0603 [SMD]"]
  R8 = Resistor [tolerance=±5% resistance=100 package="0603 [SMD]"]
  S1 = Pushbutton [package="[SMD]"]
  S2 = Pushbutton [package="[SMD]"]
  S3 = Pushbutton [package="[SMD]"]
  R9 = Resistor [tolerance=±5% resistance=100 package="0603 [SMD]"]
  R10 = Resistor [tolerance=±5% resistance=100 package="0603 [SMD]"]
  R11 = Resistor [tolerance=±5% resistance=100 package="0603 [SMD]"]

nets:
  N1: Part1.D8, R7.Pin_1
  N2: Part1.D9_PWM, R8.Pin_1
  N3: Part1.D11_PWM/MOSI, S1.Pin_3, S1.Pin_4, R9.Pin_1
  N4: Part1.D12/MISO, S2.Pin_3, S2.Pin_4, R10.Pin_1
  N5: Part1.D13/SCK, S3.Pin_3, S3.Pin_4, R11.Pin_1
  N6: Part1.GND, R9.Pin_0, R10.Pin_0, R11.Pin_0
  N7: Part1.D2, R1.Pin_1
  N8: Part1.D3_PWM, R2.Pin_1
  N9: Part1.D4, R3.Pin_1
  N10: Part1.D5_PWM, R4.Pin_1
  N11: Part1.D6_PWM, R5.Pin_1
  N12: Part1.D7, R6.Pin_1
  N13: Part1.5V, S3.Pin_1, S3.Pin_2
  N14: DI1.cathodeE, R5.Pin_0
  N15: DI1.cathodeD, R4.Pin_0
  N16: DI1.cathodeC, R3.Pin_0
  N17: DI1.cathodeDP, R8.Pin_0
  N18: DI1.cathodeB, R2.Pin_0
  N19: DI1.cathodeA, R1.Pin_0
  N20: DI1.cathodeF, R6.Pin_0
  N21: DI1.cathodeG, R7.Pin_0
  N22: S1.Pin_1, S1.Pin_2
  N23: S2.Pin_1, S2.Pin_2
